// Logisim project comparator_1bit.circ as structural Verilog
module main (
  input  Input_1,
  input  Input_2,
  output Output_1,
  output Output_2,
  output Output_3
);

  comparator1 comparator1_1 (.A(Input_1), .B(Input_2), .LESS(Output_1), .GREATER(Output_2), .EQUAL(Output_3));
endmodule

// VHDL entity comparator1, as the project stores it:
LIBRARY ieee;
USE ieee.std_logic_1164.all;

ENTITY comparator1 IS
  PORT (
	A, B: in std_logic;
	LESS, GREATER, EQUAL: out std_logic
    );
END comparator1;


ARCHITECTURE TypeArchitecture OF comparator1 IS
BEGIN
	process(A,B) 
	begin
		if A < B then 
			LESS <= '1';
			GREATER <= '0';
			EQUAL <= '0';
		elsif A > B then
			GREATER <= '1';
			LESS <= '0';
			EQUAL <= '0';
		else
			LESS <= '0';
			GREATER <= '0';
			EQUAL <= '1';
		end if;
	end process;

END TypeArchitecture;
