// Logisim project comparator_1b_flux.circ as structural Verilog
module main (
  input  in_1,
  input  in_2,
  output out_3,
  output out_4,
  output out_5
);

  comparator1 comparator1_1 (.A(in_1), .B(in_2), .LESS(out_3), .GREATER(out_4), .EQUAL(out_5));
endmodule

// VHDL entity comparator1, as the project stores it:
LIBRARY ieee;
USE ieee.std_logic_1164.all;

ENTITY comparator1 IS
  PORT (
	A, B: in std_logic;
	LESS, GREATER, EQUAL: out std_logic
    );
END comparator1;


ARCHITECTURE flux OF comparator1 IS

BEGIN
	GREATER <= A and (not B);
	EQUAL <= A xnor B;
	LESS <= (not A) and B;

END flux;
